// Logisim project ejemploPracticaFinal3.circ as structural Verilog: 9 circuits, main circuit main
module main (
  input  [1:0] in_1,
  input  E1,
  input  E2,
  input  E3,
  input  E4,
  input  [1:0] in_6,
  input  [3:0] A,
  input  [3:0] B,
  input  in_9,
  output out_10,
  output [3:0] out_11,
  output out_12
);

  mux mux_1 (.E0(E1), .E1(E2), .E2(E3), .E3(E4), .code(in_1), .Out(out_10));
  alu4 alu4_1 (.A(A), .B(B), .Cinit(in_9), .in_1(in_6), .out(out_11), .overflow(out_12));
endmodule

module fullAdder (
  input  A,
  input  B,
  input  Cin,
  output A_B,
  output Cout
);

  wire and_1_out, and_2_out, xor_1_out;

  xor xor_1 (xor_1_out, A, B);
  xor xor_2 (A_B, xor_1_out, Cin);
  and and_1 (and_1_out, A, B);
  or or_1 (Cout, and_1_out, and_2_out);
  and and_2 (and_2_out, xor_1_out, Cin);
endmodule

module decode (
  input  [1:0] code,
  output s0,
  output s1,
  output s2,
  output s3
);

  wire not_1_out, not_2_out;

  not not_1 (not_1_out, code[0]);
  not not_2 (not_2_out, code[1]);
  and and_1 (s0, not_1_out, not_2_out);
  and and_2 (s1, code[0], not_2_out);
  and and_3 (s2, not_1_out, code[1]);
  and and_4 (s3, code[0], code[1]);
endmodule

module mux (
  input  [1:0] code,
  input  E0,
  input  E1,
  input  E2,
  input  E3,
  output Out
);

  wire and_1_out, and_2_out, and_3_out, and_4_out, decode_1_s0, decode_1_s1, decode_1_s2, decode_1_s3;

  decode decode_1 (.code(code), .s0(decode_1_s0), .s1(decode_1_s1), .s2(decode_1_s2), .s3(decode_1_s3));
  and and_1 (and_1_out, decode_1_s0, E0);
  and and_2 (and_2_out, E1, decode_1_s1);
  and and_3 (and_3_out, E3, decode_1_s3);
  and and_4 (and_4_out, E2, decode_1_s2);
  or or_1 (Out, and_1_out, and_2_out, and_4_out, and_3_out);
endmodule

module mux1_5 (
  input  D0,
  input  D1,
  input  D2,
  input  D3,
  input  E0,
  input  E1,
  input  E2,
  input  E3,
  output Out
);

  wire and_1_out, and_2_out, and_3_out, and_4_out;

  and and_1 (and_1_out, D0, E0);
  and and_2 (and_2_out, E1, D1);
  and and_3 (and_3_out, E3, D3);
  and and_4 (and_4_out, E2, D2);
  or or_1 (Out, and_1_out, and_2_out, and_4_out, and_3_out);
endmodule

module mux2_6 (
  input  [1:0] in_1,
  input  E0,
  input  E1,
  input  E2,
  input  E3,
  output out_6
);

  wire decode_1_s0, decode_1_s1, decode_1_s2, decode_1_s3;

  decode decode_1 (.code(in_1), .s0(decode_1_s0), .s1(decode_1_s1), .s2(decode_1_s2), .s3(decode_1_s3));
  mux1_5 mux1_5_1 (
    .D0(decode_1_s0), .D1(decode_1_s1), .D2(decode_1_s2), .D3(decode_1_s3), .E0(E0), .E1(E1), .E2(E2),
    .E3(E3), .Out(out_6));
endmodule

module Alu1 (
  input  [1:0] in_1,
  input  A,
  input  B,
  input  Cin,
  output out,
  output Cout
);

  wire and_1_out, fulladder_1_a_b, not_1_out, or_1_out;

  and and_1 (and_1_out, A, B);
  fullAdder fulladder_1 (.A(A), .B(B), .Cin(Cin), .A_B(fulladder_1_a_b), .Cout(Cout));
  not not_1 (not_1_out, A);
  or or_1 (or_1_out, A, B);
  mux mux_1 (.E0(and_1_out), .E1(or_1_out), .E2(not_1_out), .E3(fulladder_1_a_b), .code(in_1), .Out(out));
endmodule

module alu4 (
  input  [1:0] in_1,
  input  [3:0] A,
  input  [3:0] B,
  input  Cinit,
  output [3:0] out,
  output overflow
);

  wire alu1_1_cout, alu1_2_cout, alu1_4_cout;

  Alu1 alu1_1 (.A(A[0]), .B(B[0]), .Cin(Cinit), .in_1(in_1), .out(out[0]), .Cout(alu1_1_cout));
  Alu1 alu1_2 (.A(A[1]), .B(B[1]), .Cin(alu1_1_cout), .in_1(in_1), .out(out[1]), .Cout(alu1_2_cout));
  Alu1 alu1_3 (.A(A[3]), .B(B[3]), .Cin(alu1_4_cout), .in_1(in_1), .out(out[3]), .Cout(overflow));
  Alu1 alu1_4 (.A(A[2]), .B(B[2]), .Cin(alu1_2_cout), .in_1(in_1), .out(out[2]), .Cout(alu1_4_cout));
endmodule

module malSub (
  input  [3:0] A,
  input  [3:0] B,
  output [3:0] out_3
);

  wire [3:0] adder_1_out, not_1_out;

  assign not_1_out = ~B;  // NOT_Gate not_1, 4 bits wide
  Adder #(.width(4)) adder_1 (.a(not_1_out), .b(4'b0001), .out(adder_1_out));  // open: cin, cout
  Adder #(.width(4)) adder_2 (.a(A), .b(adder_1_out), .out(out_3));  // open: cin, cout
endmodule
