// Logisim project main.circ as structural Verilog: 16 circuits, main circuit main
module main (
  input  in_1,
  output out_2
);

  // not not_1: pin names not known; wires that end beside it: in_1, out_2
endmodule

module \and  (
  input  X,
  input  Y,
  output out_3
);

  wire transistor_1_out;

  Transistor #(.\type ("n")) transistor_1 (.in(1'b1), .out(transistor_1_out), .gate(X));
  Transistor #(.\type ("n")) transistor_2 (.in(transistor_1_out), .out(out_3), .gate(Y));
  Transistor transistor_3 (.in(1'b0), .out(out_3), .gate(Y));
  Transistor transistor_4 (.in(1'b0), .out(out_3), .gate(X));
endmodule

module \or  (
  input  X,
  input  Y,
  output out_3
);

  wire transistor_3_out;

  Transistor #(.\type ("n")) transistor_1 (.in(1'b1), .out(out_3), .gate(X));
  Transistor transistor_2 (.in(transistor_3_out), .out(out_3), .gate(X));
  Transistor transistor_3 (.in(1'b0), .out(transistor_3_out), .gate(Y));
  Transistor #(.\type ("n")) transistor_4 (.in(1'b1), .out(out_3), .gate(Y));
endmodule

module \not  (
  input  X,
  output out_2
);

  Transistor transistor_1 (.in(1'b1), .out(out_2), .gate(X));
  Transistor #(.\type ("n")) transistor_2 (.in(1'b0), .out(out_2), .gate(X));
endmodule

module Xand (
  input  X,
  input  Y,
  output out_3
);

  wire transistor_3_out;

  Transistor transistor_1 (.in(1'b1), .out(out_3), .gate(X));
  Transistor #(.\type ("n")) transistor_2 (.in(transistor_3_out), .out(out_3), .gate(X));
  Transistor #(.\type ("n")) transistor_3 (.in(1'b0), .out(transistor_3_out), .gate(Y));
  Transistor transistor_4 (.in(1'b1), .out(out_3), .gate(Y));
endmodule

module Xor (
  input  X,
  input  Y,
  output out_3
);

  wire transistor_1_out;

  Transistor transistor_1 (.in(1'b1), .out(transistor_1_out), .gate(X));
  Transistor transistor_2 (.in(transistor_1_out), .out(out_3), .gate(Y));
  Transistor #(.\type ("n")) transistor_3 (.in(1'b0), .out(out_3), .gate(Y));
  Transistor #(.\type ("n")) transistor_4 (.in(1'b0), .out(out_3), .gate(X));
endmodule

module NO_A___O_B (
  input  A,
  input  B,
  output out_3
);

  wire not_1_out_2;

  \not  not_1 (.X(A), .out_2(not_1_out_2));
  \or  or_1 (.X(not_1_out_2), .Y(B), .out_3(out_3));
endmodule

module A_Y___NO_B_____O_____NO_A___Y_B (
  input  A,
  input  B,
  output out_3
);

  wire and_1_out_3, and_2_out_3, not_1_out_2, not_2_out_2;

  \not  not_1 (.X(A), .out_2(not_1_out_2));
  \not  not_2 (.X(B), .out_2(not_2_out_2));
  \and  and_1 (.X(not_2_out_2), .Y(A), .out_3(and_1_out_3));
  \and  and_2 (.X(B), .Y(not_1_out_2), .out_3(and_2_out_3));
  \or  or_1 (.X(and_2_out_3), .Y(and_1_out_3), .out_3(out_3));
endmodule

module PRIMOS (
  input  E4,
  input  E3,
  input  E1,
  input  E0,
  output out_5
);

  wire and_1_out_5, and_2_out_5, and_3_out_5, and_4_out_5, and_5_out_5, and_6_out_5, not_1_out_2,
       not_2_out_2, not_3_out_2, not_4_out_2;

  \not  not_1 (.X(E4), .out_2(not_1_out_2));
  \not  not_2 (.X(E3), .out_2(not_2_out_2));
  \not  not_3 (.X(E1), .out_2(not_3_out_2));
  \not  not_4 (.X(E0), .out_2(not_4_out_2));
  AND and_1 (.X(not_4_out_2), .Y(E1), .X_prime(not_2_out_2), .Y_prime(not_1_out_2), .out_5(and_1_out_5));
  AND and_2 (.X(E0), .Y(E1), .X_prime(not_2_out_2), .Y_prime(not_1_out_2), .out_5(and_2_out_5));
  AND and_3 (.X(E0), .Y(not_3_out_2), .X_prime(E3), .Y_prime(not_1_out_2), .out_5(and_3_out_5));
  _6OR u_6or_1 (
    .X(and_5_out_5), .Y(and_6_out_5), .X_prime(and_4_out_5), .Y_prime(and_3_out_5),
    .X_prime_prime(and_2_out_5), .Y_prime_prime(and_1_out_5), .out_7(out_5));
  AND and_4 (.X(E0), .Y(E1), .X_prime(E3), .Y_prime(not_1_out_2), .out_5(and_4_out_5));
  AND and_5 (.X(E0), .Y(not_3_out_2), .X_prime(E3), .Y_prime(E4), .out_5(and_5_out_5));
  AND and_6 (.X(E0), .Y(E1), .X_prime(not_2_out_2), .Y_prime(E4), .out_5(and_6_out_5));
endmodule

module OR (
  input  X,
  input  Y,
  input  X_prime,
  input  Y_prime,
  output out_5
);

  wire transistor_3_out, transistor_4_out, transistor_5_out;

  Transistor #(.\type ("n")) transistor_1 (.in(1'b1), .out(out_5), .gate(X));
  Transistor transistor_2 (.in(transistor_3_out), .out(out_5), .gate(X));
  Transistor transistor_3 (.in(transistor_4_out), .out(transistor_3_out), .gate(Y));
  Transistor transistor_4 (.in(transistor_5_out), .out(transistor_4_out), .gate(X_prime));
  Transistor transistor_5 (.in(1'b0), .out(transistor_5_out), .gate(Y_prime));
  Transistor #(.\type ("n")) transistor_6 (.in(1'b1), .out(out_5), .gate(Y));
  Transistor #(.\type ("n")) transistor_7 (.in(1'b1), .out(out_5), .gate(X_prime));
  Transistor #(.\type ("n")) transistor_8 (.in(1'b1), .out(out_5), .gate(Y_prime));
endmodule

module AND (
  input  X,
  input  Y,
  input  X_prime,
  input  Y_prime,
  output out_5
);

  wire transistor_1_out, transistor_2_out, transistor_3_out;

  Transistor #(.\type ("n")) transistor_1 (.in(1'b1), .out(transistor_1_out), .gate(X));
  Transistor #(.\type ("n")) transistor_2 (.in(transistor_1_out), .out(transistor_2_out), .gate(Y));
  Transistor #(.\type ("n")) transistor_3 (.in(transistor_2_out), .out(transistor_3_out), .gate(X_prime));
  Transistor #(.\type ("n")) transistor_4 (.in(transistor_3_out), .out(out_5), .gate(Y_prime));
  Transistor transistor_5 (.in(1'b0), .out(out_5), .gate(Y));
  Transistor transistor_6 (.in(1'b0), .out(out_5), .gate(X_prime));
  Transistor transistor_7 (.in(1'b0), .out(out_5), .gate(Y_prime));
  Transistor transistor_8 (.in(1'b0), .out(out_5), .gate(X));
endmodule

module _6OR (
  input  X,
  input  Y,
  input  X_prime,
  input  Y_prime,
  input  X_prime_prime,
  input  Y_prime_prime,
  output out_7
);

  wire transistor_3_out, transistor_4_out, transistor_5_out, transistor_6_out, transistor_7_out;

  Transistor #(.\type ("n")) transistor_1 (.in(1'b1), .out(out_7), .gate(X));
  Transistor transistor_2 (.in(transistor_3_out), .out(out_7), .gate(X));
  Transistor transistor_3 (.in(transistor_4_out), .out(transistor_3_out), .gate(Y));
  Transistor transistor_4 (.in(transistor_5_out), .out(transistor_4_out), .gate(X_prime));
  Transistor transistor_5 (.in(transistor_6_out), .out(transistor_5_out), .gate(Y_prime));
  Transistor transistor_6 (.in(transistor_7_out), .out(transistor_6_out), .gate(X_prime_prime));
  Transistor transistor_7 (.in(1'b0), .out(transistor_7_out), .gate(Y_prime_prime));
  Transistor #(.\type ("n")) transistor_8 (.in(1'b1), .out(out_7), .gate(Y));
  Transistor #(.\type ("n")) transistor_9 (.in(1'b1), .out(out_7), .gate(X_prime));
  Transistor #(.\type ("n")) transistor_10 (.in(1'b1), .out(out_7), .gate(Y_prime));
  Transistor #(.\type ("n")) transistor_11 (.in(1'b1), .out(out_7), .gate(X_prime_prime));
  Transistor #(.\type ("n")) transistor_12 (.in(1'b1), .out(out_7), .gate(Y_prime_prime));
endmodule

module COMPLEMENTO_A_2 (
  input  E2,
  input  E1,
  input  E0,
  output S2,
  output S1,
  output S0
);

  wire not_1_out_2, not_2_out_2, not_3_out_2, not_4_out, not_5_out;

  \not  not_1 (.X(E2), .out_2(not_1_out_2));
  \not  not_2 (.X(E1), .out_2(not_2_out_2));
  \not  not_3 (.X(E0), .out_2(not_3_out_2));
  not not_4 (not_4_out, S1);
  or_Exclusivo or_exclusivo_1 (.X(not_4_out), .Y(not_1_out_2), .out_3(S2));
  not not_5 (not_5_out, S0);
  or_Exclusivo or_exclusivo_2 (.X(1'b1), .Y(not_3_out_2), .out_3(S0));
  or_Exclusivo or_exclusivo_3 (.X(not_5_out), .Y(not_2_out_2), .out_3(S1));
endmodule

module Pruebas (
  input  X,
  input  Y,
  output out_3
);

  wire and_1_out_3, and_2_out_3, not_1_out_2, not_2_out_2;

  \not  not_1 (.X(X), .out_2(not_1_out_2));
  \not  not_2 (.X(Y), .out_2(not_2_out_2));
  \and  and_1 (.X(Y), .Y(not_1_out_2), .out_3(and_1_out_3));
  \and  and_2 (.X(X), .Y(not_2_out_2), .out_3(and_2_out_3));
  \or  or_1 (.X(and_2_out_3), .Y(and_1_out_3), .out_3(out_3));
endmodule

module prubas_2 (
  input  E2,
  input  E1,
  input  E0,
  output S2,
  output S1,
  output S0
);

  wire not_1_out_2, not_2_out_2, not_3_out_2, not_4_out, not_5_out;

  \not  not_1 (.X(E2), .out_2(not_1_out_2));
  \not  not_2 (.X(E1), .out_2(not_2_out_2));
  \not  not_3 (.X(E0), .out_2(not_3_out_2));
  not not_4 (not_4_out, S1);
  or_Exclusivo or_exclusivo_1 (.X(not_4_out), .Y(not_1_out_2), .out_3(S2));
  not not_5 (not_5_out, S0);
  or_Exclusivo or_exclusivo_2 (.X(not_5_out), .Y(not_2_out_2), .out_3(S1));
  or_Exclusivo or_exclusivo_3 (.X(1'b1), .Y(not_3_out_2), .out_3(S0));
endmodule

// OR X
module or_Exclusivo (
  input  X,
  input  Y,
  output out_3
);

  wire and_1_out_3, and_2_out_3, not_1_out_2, not_2_out_2;

  \not  not_1 (.X(X), .out_2(not_1_out_2));
  \not  not_2 (.X(Y), .out_2(not_2_out_2));
  \and  and_1 (.X(Y), .Y(not_1_out_2), .out_3(and_1_out_3));
  \and  and_2 (.X(X), .Y(not_2_out_2), .out_3(and_2_out_3));
  \or  or_1 (.X(and_2_out_3), .Y(and_1_out_3), .out_3(out_3));
endmodule
